# Fritzing sketch UselessDevice (saved by Fritzing 0.9.3b)

parts:
  Arduino = Arduino Nano (Rev3.0)
  Lid_Servo = Basic Servo
  Arm_Servo = Basic Servo
  Flag_Servo = Basic Servo
  Toggle_Switch = Toggle Switch [package=THT]
  Power_Switch = Toggle Switch [package=THT]
  VCC1 = Battery block 9V

nets:
  GND: Arduino.GND, Lid_Servo.gnd, Arm_Servo.gnd, Flag_Servo.gnd, Toggle_Switch.L2, VCC1.-
  N1: Arduino.D3, Lid_Servo.pulse
  N2: Arduino.D5, Arm_Servo.pulse
  N3: Arduino.D7, Toggle_Switch.COM
  N4: Arduino.D12/MISO, Flag_Servo.pulse
  N5: Arduino.VIN, Power_Switch.COM
  VCC: Arduino.5V, Lid_Servo.vcc, Arm_Servo.vcc, Flag_Servo.vcc
  N6: Power_Switch.L1, VCC1.+
